// Logisim project SAP1_versao6.circ as structural Verilog: 19 circuits, main circuit Microprocessador-SPA
module Main (
  input  CLK,
  input  CLR,
  output [3:0] Dados,
  output [3:0] \Dados_Endereçoes ,
  output [3:0] Dados_2,
  output [3:0] \Dados_Endereçoes_2 
);

  wire buffer_1_out, buffer_2_out, buffer_3_out, buffer_4_out, Out_Tx1, Out_Tx2, Tx1, Tx2;
  wire [3:0] counter_1_q, counter_1_q_2;

  Microprocessador_SPA microprocessador_spa_1 (
    .Dados(Dados), .Reset(CLR), .\Dados___Endereços (\Dados_Endereçoes ), .In_Rx(buffer_1_out),
    .Out_Tx(Out_Tx1), .CLK(CLK), .Rx(buffer_2_out), .Tx(Tx1));  // open: Dado, Pos
  buf buffer_1 (buffer_1_out, Out_Tx2);
  buf buffer_2 (buffer_2_out, Tx2);
  Shift_Register #(.length(4)) shift_register_1 (
    .in(Out_Tx1), .clk(CLK));  // open: shift, out, load, clr, d0, q0, d1, q1, d2, q2, d3, q3
  buf buffer_3 (buffer_3_out, Out_Tx1);
  Microprocessador_SPA microprocessador_spa_2 (
    .Dados(Dados_2), .Reset(CLR), .\Dados___Endereços (\Dados_Endereçoes_2 ), .In_Rx(buffer_3_out),
    .Out_Tx(Out_Tx2), .CLK(CLK), .Rx(buffer_4_out), .Tx(Tx2));  // open: Dado, Pos
  buf buffer_4 (buffer_4_out, Tx1);
  Hex_Digit_Display hex_digit_display_1 (.value(counter_1_q_2));  // open: dp
  Counter counter_1 (.Q({counter_1_q_2, counter_1_q}), .clk(CLK), .clr(CLR));  // open: load, D, count, carry
  Hex_Digit_Display hex_digit_display_2 (.value(counter_1_q));  // open: dp
endmodule

module Microprocessador_SPA (
  input  [3:0] Pos,
  input  In_Rx,
  input  [7:0] Dado,
  input  Rx,
  input  Reset,
  input  CLK,
  output [3:0] Dados,
  output [3:0] \Dados___Endereços ,
  output Out_Tx,
  output Tx
);

  wire and_1_out, buffer_1_out, CLK_t, clk_t_t, Clock_out, Cmp, controlador_sequencializador_rom_1_hlt, Cp,
       Ea, Ep, Erx, Eu, Halt, In, IncDec, Lp, Ltx, Mul, nCE, nEi, nLa, nLb, nLi, nLm, nLo, not_1_out,
       not_2_out, not_3_out, not_4_out, not_5_out, Np, pause, RDnWR, \registrador_instruções_1_i4 ,
       \registrador_instruções_1_i5 , \registrador_instruções_1_i6 , \registrador_instruções_1_i7 ,
       somador_subtrator_1_out_9, somador_subtrator_1_out_10, somador_subtrator_1_out_11, Su,
       temporizador_1_halt, Tm, \unidade_de_comunicação_serial_1_hlt ;
  wire [3:0] controlled_buffer_1_out, rem_1_remout, temporizador_1_show,
       \unidade_de_comunicação_serial_1_dataout ;
  wire [7:0] acumulador_1_a_out_ula, counter_1_q, \indicação_visual_1_output , registrador_b_1_b_dataout;

  Clock Clock (.out(Clock_out));
  assign controlled_buffer_1_out = In ? Pos : 4'bz;  // Controlled_Buffer controlled_buffer_1
  assign CLK_t = and_1_out ? clk_t_t : 1'bz;  // Controlled_Buffer controlled_buffer_2
  or or_1 (clk_t_t, Clock_out, CLK);
  and and_1 (and_1_out, not_4_out, pause, Halt);
  not not_1 (not_1_out, CLK_t);
  not not_2 (not_2_out, Reset);
  not not_3 (not_3_out, nCE);
  Controlador_Sequencializador_ROM controlador_sequencializador_rom_1 (
    .I7(\registrador_instruções_1_i7 ), ._16(\registrador_instruções_1_i6 ),
    .I5(\registrador_instruções_1_i5 ), .I4(\registrador_instruções_1_i4 ), .Cp(Cp), .Ep(Ep), .nLm(nLm),
    .nCE(nCE), .nLl(nLi), .nEi(nEi), .nLa(nLa), .Ea(Ea), .Su(Su), .Eu(Eu), .nLb(nLb), .nLo(nLo),
    .IncDec(IncDec), .RDnWR(RDnWR), .Mul(Mul), .Lp(Lp), .HLT(controlador_sequencializador_rom_1_hlt),
    .CLK(CLK_t), .CLR(Reset), .Tx(Tx), .Np_2(Np), .Erx(Erx), .Ltx(Ltx), .NP(buffer_1_out), .Tm(Tm), .In(In),
    .Cmp(Cmp));
  not not_4 (not_4_out, controlador_sequencializador_rom_1_hlt);
  REM rem_1 (.in_1(\Dados___Endereços ), .nLm(nLm), .CLK(CLK_t), .REMOut(rem_1_remout));
  not not_5 (not_5_out, In);
  assign controlled_buffer_1_out = not_5_out ? rem_1_remout : 4'bz;  // Controlled_Buffer controlled_buffer_3
  Contador_Programa contador_programa_1 (
    .Cp(Cp), .nCLK(not_1_out), .nCLR(not_2_out), .Ep(Ep), .Cp_Out(\Dados___Endereços ), .Lp(Lp),
    .Cp_In(\Dados___Endereços ));
  \Memória_RAM  \memória_ram_1  (
    .Pos(controlled_buffer_1_out), .nCE(not_3_out), .CLK(CLK_t), .RD_nWR(RDnWR),
    .in_2({Dados, \Dados___Endereços }), .out_8({Dados, \Dados___Endereços }), .In(In), .Dados(Dado));
  \Registrador_Instruções  \registrador_instruções_1  (
    .in_1({Dados, \Dados___Endereços }), .nLi(nLi), .CLK(CLK_t), .CLR(Reset), .nEi(nEi),
    .out_6(\Dados___Endereços ), .I4(\registrador_instruções_1_i4 ), .I5(\registrador_instruções_1_i5 ),
    .I6(\registrador_instruções_1_i6 ), .I7(\registrador_instruções_1_i7 ));
  buf buffer_1 (buffer_1_out, Np);
  Hex_Digit_Display hex_digit_display_1 (.value(temporizador_1_show));  // open: dp
  Hex_Digit_Display hex_digit_display_2 (.value(\unidade_de_comunicação_serial_1_dataout ));  // open: dp
  not not_6 (Halt, \unidade_de_comunicação_serial_1_hlt );
  Hex_Digit_Display hex_digit_display_3 (.value(counter_1_q[7:4]));  // open: dp
  Counter counter_1 (.Q(counter_1_q), .clk(clk_t_t), .clr(Reset));  // open: load, D, count, carry
  Acumulador acumulador_1 (
    .A_In({Dados, \Dados___Endereços }), .nLa(nLa), .CLK(CLK_t), .Ea(Ea), .A_Out_ULA(acumulador_1_a_out_ula),
    .A_Out({Dados, \Dados___Endereços }));
  Somador_Subtrator somador_subtrator_1 (
    .Su(Su), .B_data(registrador_b_1_b_dataout), .A_dataOut2({Dados, \Dados___Endereços }),
    .A_data(acumulador_1_a_out_ula), .Eu(Eu), .IncDec(IncDec), .mul(Mul), .out_9(somador_subtrator_1_out_9),
    .out_10(somador_subtrator_1_out_10), .out_11(somador_subtrator_1_out_11), .Cmp(Cmp));
  Registrador_B registrador_b_1 (
    .B_dataIn({Dados, \Dados___Endereços }), .B_dataOut(registrador_b_1_b_dataout), .nLb(nLb), .CLK(CLK_t));
  not not_7 (pause, temporizador_1_halt);
  \Indicação_Visual  \indicação_visual_1  (
    .Input({Dados, \Dados___Endereços }), .Output(\indicação_visual_1_output ), .nLo(nLo), .CLK(CLK_t),
    .CLR(Reset));
  Hex_Digit_Display hex_digit_display_4 (.value(counter_1_q[3:0]));  // open: dp
  LED led (.in(somador_subtrator_1_out_9));
  LED led_2 (.in(somador_subtrator_1_out_10));
  LED led_3 (.in(somador_subtrator_1_out_11));
  \Unidade_de_Comunicação_Serial  \unidade_de_comunicação_serial_1  (
    .Recebendo(In_Rx), .Enable_Rx(Rx), .CLK(clk_t_t), .HLT(\unidade_de_comunicação_serial_1_hlt ),
    .Transmitimos(\Dados___Endereços ), .Enable_Tx(Tx), .CLR(Reset), .Transmitido(Out_Tx), .Ltx(Ltx),
    .Erx(Erx), .DataOut(\unidade_de_comunicação_serial_1_dataout ));
  Temporizador temporizador_1 (
    .IN(\Dados___Endereços ), .CLK(clk_t_t), .Tm(Tm), .SHOW(temporizador_1_show), .Halt(temporizador_1_halt),
    .CLR(Reset));
  Hex_Digit_Display hex_digit_display_5 (.value(\indicação_visual_1_output [3:0]));  // open: dp
  Hex_Digit_Display hex_digit_display_6 (.value(\indicação_visual_1_output [7:4]));  // open: dp
  DotMatrix #(.matrixcols(8), .matrixrows(1), .dotshape("circle")) dotmatrix_1 (
    .col0(\indicação_visual_1_output [7]), .col1(\indicação_visual_1_output [6]),
    .col2(\indicação_visual_1_output [5]), .col3(\indicação_visual_1_output [4]),
    .col4(\indicação_visual_1_output [3]), .col5(\indicação_visual_1_output [2]),
    .col6(\indicação_visual_1_output [1]), .col7(\indicação_visual_1_output [0]));

  // Other names for the same wires on the sheet: CLR = Reset; In_Ativado = In

  // Notes on the sheet:
  //   SAP-1 EM LOGISIM Modificado Cláudio - Versão 6 (2025)
  //   Arquitetura de Computadores I
  //   Grupo:
  //   Instruções:
  //   LDA 0000: A<-*(MEM) (load accumulator)
  //   ADD 0001: A<-A+B
  //   SUB 0010: A<-A-B
  //   INC 0011: A<=A+1
  //   DEC 0100: A<=A-1
  //   MUL 0101: A<-AxB
  //   JMP 0110: CP<-endereço de salto
  //   STO 0111: *(MEM)<-A (store accumulator)
  //   TX 1000 tx <- O que vai ser transmitido
  //   OUT 1110: exibir o valor
  //   HLT 1111: interromper o circuito
  //   Como usar:
  //   Adicione as operações no bloco de memória RAM,
  //   execute um RESET e envie pulsos de clock.
  //   Esse trabalho foi uma modificação do trabalho feito por:
  //   - André Luís Silva de Paula
  //   - André Santos Alves
  //   - Nathan de Araújo Cunha Lisboa
  //   - Pedro Malta Boscatti
  //   - Sophia Damasceno Satuf
  //   As modificações foram feitas no controlador sequencializador.
  //   Com as alterações agora o controlador é implementado usando
  //   ROMs e possui ciclo variavél de máquina.
  //   Esse trabalho foi uma modificação do trabalho feito por:
  //   RX 1001 Recebe o que vai ser transmitido
  //   CMP 1010 Compara o Acumulador e o Cp 
  //   - Heitor Viana Bastos
  //   - Leonardo Braga de Oliveira
  //   TMP 1011 Cp <- Da uma pausa por esse número de clocks
  //   IN 1100 Permite a inserção direta na memória RAM
  //   - Thiago Henrique Gomes Felicano
  //   - Rafael Fonseca Cairicatti Bezerira
  //   - Yasmin Torres Moreira dos Santos
endmodule

module Contador_Programa (
  input  Lp,
  input  [3:0] Cp_In,
  input  Cp,
  input  nCLK,
  input  nCLR,
  input  Ep,
  output [3:0] Cp_Out
);

  wire not_1_out;
  wire [3:0] counter_1_q;

  not not_1 (not_1_out, nCLR);
  Counter #(.width(4), .max('hf), .trigger("falling")) counter_1 (
    .load(Lp), .D(Cp_In), .count(Cp), .Q(counter_1_q), .clk(nCLK), .clr(not_1_out));  // open: carry
  assign Cp_Out = Ep ? counter_1_q : 4'bz;  // Controlled_Buffer controlled_buffer_1
endmodule

module REM (
  input  [3:0] in_1,
  input  nLm,
  input  CLK,
  output [3:0] REMOut
);

  wire not_1_out;

  not not_1 (not_1_out, nLm);
  Register #(.width(4)) register_1 (.D(in_1), .en(not_1_out), .Q(REMOut), .clk(CLK));  // open: clr
endmodule

module \Memória_RAM  (
  input  [7:0] Dados,
  input  [7:0] in_2,
  input  [3:0] Pos,
  input  In,
  input  nCE,
  input  CLK,
  input  RD_nWR,
  output [7:0] out_8
);

  wire not_1_out, or_1_out;
  wire [7:0] controlled_buffer_1_out;

  or or_1 (or_1_out, In, nCE);
  assign controlled_buffer_1_out = In ? Dados : 8'bz;  // Controlled_Buffer controlled_buffer_1
  RAM #(.addrWidth(4)) ram_1 (
    .addr(Pos), .data(controlled_buffer_1_out), .sel(or_1_out), .clk(CLK), .ld(RD_nWR), .clr(1'b0));
  assign controlled_buffer_1_out = not_1_out ? in_2 : 8'bz;  // Controlled_Buffer controlled_buffer_2
  assign out_8 = RD_nWR ? controlled_buffer_1_out : 8'bz;  // Controlled_Buffer controlled_buffer_3
  not not_1 (not_1_out, RD_nWR);

  // Notes on the sheet:
  //   Programas Exemplo
  //   Exemplo 1:  02 + 03 - 04 + 02 = 03
  //   0f e0 1e e0 2d e0 1f e0 f0 00 00 00 00 04 03 02
  //   Exemplo 2:  150 + 70 - 50 + 100 = ? 270
  //   0f e0 1e e0 2d e0 1c e0 f0 00 00 00 64 32 46 96
  //   Exemplo 3:  5 x 2 - 1 - 2 + 1 = 8
  //   0f e0 5e e0 40 e0 2e e0 30 e0 f0 00 00 00 02 05
  //   Exemplo 4:  Carrega A=1,Exibe A, Inc A, Exibe A, JMP para Inc A 
  //   0f e0 30 e0 62 f0
  //   Exemplo 5:  Contador Progressivo 
  //   Exemplo 6:  Gera a Série de Fibonacci 
  //   Exemplo 7:  Série de Fibonacci - Pedro Simões
  //    Click com o botão direito do mouse sobre a RAM e carregue alguma programação disponivel
endmodule

module \Registrador_Instruções  (
  input  [7:0] in_1,
  input  nLi,
  input  CLK,
  input  CLR,
  input  nEi,
  output [3:0] out_6,
  output I4,
  output I5,
  output I6,
  output I7
);

  wire not_1_out, not_2_out;
  wire [3:0] register_1_q;

  not not_1 (not_1_out, nLi);
  not not_2 (not_2_out, nEi);
  Register register_1 (.D(in_1), .en(not_1_out), .Q({I7, I6, I5, I4, register_1_q}), .clk(CLK), .clr(CLR));
  assign out_6 = not_2_out ? register_1_q : 4'bz;  // Controlled_Buffer controlled_buffer_1
endmodule

module Acumulador (
  input  [7:0] A_In,
  input  nLa,
  input  CLK,
  input  Ea,
  output [7:0] A_Out_ULA,
  output [7:0] A_Out
);

  wire not_1_out;

  not not_1 (not_1_out, nLa);
  Register register_1 (.D(A_In), .en(not_1_out), .Q(A_Out_ULA), .clk(CLK));  // open: clr
  assign A_Out = Ea ? A_Out_ULA : 8'bz;  // Controlled_Buffer controlled_buffer_1
endmodule

module Somador_Subtrator (
  input  Su,
  input  IncDec,
  input  [7:0] B_data,
  input  [7:0] A_data,
  input  Eu,
  input  mul,
  input  Cmp,
  output [7:0] A_dataOut2,
  output out_9,
  output out_10,
  output out_11
);

  wire not_1_out;
  wire [7:0] adder_1_out, controlled_buffer_1_out, controlled_buffer_3_out, controlled_buffer_4_out,
       multiplier_1_out, xor_1_out;

  not not_1 (not_1_out, IncDec);
  assign controlled_buffer_1_out = IncDec ? 8'h1 : 8'bz;  // Controlled_Buffer controlled_buffer_1
  assign controlled_buffer_1_out = not_1_out ? B_data : 8'bz;  // Controlled_Buffer controlled_buffer_2
  assign xor_1_out = {8{Su}} ^ controlled_buffer_1_out;  // XOR_Gate xor_1, 8 bits wide
  assign controlled_buffer_3_out = Cmp ? A_data : 8'bz;  // Controlled_Buffer controlled_buffer_3
  assign controlled_buffer_4_out = Cmp ? controlled_buffer_1_out : 8'bz;  // Controlled_Buffer controlled_buffer_4
  Adder adder_1 (.a(xor_1_out), .b(A_data), .out(adder_1_out), .cin(Su));  // open: cout
  Multiplier multiplier_1 (.a(B_data), .b(A_data), .out(multiplier_1_out));  // open: cin, cout
  Comparator comparator_1 (
    .a(controlled_buffer_3_out), .b(controlled_buffer_4_out), .gt(out_9), .eq(out_10), .lt(out_11));
  assign A_dataOut2 = Eu ? adder_1_out : 8'bz;  // Controlled_Buffer controlled_buffer_5
  assign A_dataOut2 = mul ? multiplier_1_out : 8'bz;  // Controlled_Buffer controlled_buffer_6
endmodule

module Registrador_B (
  input  [7:0] B_dataIn,
  input  nLb,
  input  CLK,
  output [7:0] B_dataOut
);

  wire not_1_out;

  Register register_1 (.D(B_dataIn), .en(not_1_out), .Q(B_dataOut), .clk(CLK));  // open: clr
  not not_1 (not_1_out, nLb);
endmodule

module Decodificador (
  input  l7,
  input  l6,
  input  l5,
  input  l4,
  output LDA,
  output ADD,
  output SUB,
  output OUT,
  output HLT
);

  wire and_1_out, and_2_out, and_3_out, and_4_out, and_5_out, not_1_out, not_2_out, not_3_out, not_4_out;

  not not_1 (not_1_out, l7);
  not not_2 (not_2_out, l6);
  not not_3 (not_3_out, l5);
  not not_4 (not_4_out, l4);
  and and_1 (and_1_out, not_1_out, not_2_out, not_3_out, not_4_out);
  buf buffer_1 (LDA, and_1_out);
  buf buffer_2 (ADD, and_2_out);
  and and_2 (and_2_out, not_1_out, not_2_out, not_3_out, l4);
  buf buffer_3 (SUB, and_3_out);
  and and_3 (and_3_out, not_1_out, not_2_out, l5, not_4_out);
  buf buffer_4 (OUT, and_4_out);
  and and_4 (and_4_out, l7, l6, l5, not_4_out);
  buf buffer_5 (HLT, and_5_out);
  and and_5 (and_5_out, l7, l6, l5, l4);
endmodule

module \Indicação_Visual  (
  input  [7:0] Input,
  input  nLo,
  input  CLK,
  input  CLR,
  output [7:0] Output
);

  wire not_1_out;

  not not_1 (not_1_out, nLo);
  Register register_1 (.D(Input), .en(not_1_out), .Q(Output), .clk(CLK), .clr(CLR));
endmodule

module Controlador_Sequencializador_ROM (
  input  I7,
  input  _16,
  input  I5,
  input  I4,
  input  CLK,
  input  CLR,
  input  NP,
  output Cp,
  output Ep,
  output nLm,
  output nCE,
  output nLl,
  output nEi,
  output nLa,
  output Ea,
  output Su,
  output Eu,
  output nLb,
  output nLo,
  output IncDec,
  output RDnWR,
  output Mul,
  output Lp,
  output Np_2,
  output Tx,
  output Erx,
  output Ltx,
  output In,
  output Tm,
  output Cmp,
  output HLT
);

  wire clr_t, d_ff_1_q, load, nor_1_out, not_1_out, not_2_out, or_1_out, or_2_out, shift_register_1_q0,
       shift_register_1_q1, shift_register_1_q3, shift_register_1_q4;
  wire [0:0] rom_2_data;
  wire [4:0] counter_1_q, rom_1_data;

  and and_1 (HLT, I7, _16, I5, I4);
  or or_1 (or_1_out, NP, Np_2);
  D_Flip_Flop d_ff_1 (.clk(CLK), .D(or_1_out), .Q(d_ff_1_q));  // open: Qn, preset, en, reset
  ROM #(.addrWidth(4), .dataWidth(5)) rom_1 (.addr({I7, _16, I5, I4}), .data(rom_1_data));  // open: sel
  or or_2 (or_2_out, CLR, d_ff_1_q);
  or or_3 (clr_t, or_2_out, nor_1_out);
  Counter #(.width(5), .max('h1f), .ongoal("continue")) counter_1 (
    .load(load), .D(rom_1_data), .count(not_1_out), .Q(counter_1_q), .clk(not_2_out), .clr(clr_t));  // open: carry
  not not_1 (not_1_out, load);
  not not_2 (not_2_out, CLK);
  Shift_Register #(.length(6)) shift_register_1 (
    .in(nor_1_out), .clk(CLK), .clr(or_2_out), .q0(shift_register_1_q0), .q1(shift_register_1_q1), .q2(load),
    .q3(shift_register_1_q3), .q4(shift_register_1_q4));  // open: shift, out, load, d0, d1, d2, d3, d4, d5, q5
  nor nor_1 (nor_1_out, shift_register_1_q0, shift_register_1_q1, load, shift_register_1_q3, shift_register_1_q4);
  ROM #(.addrWidth(5), .dataWidth(24)) rom_2 (
    .addr(counter_1_q),
    .data({Cp, Ep, nLm, nCE, nLl, nEi, nLa, Ea, Su, Eu, nLb, nLo, IncDec, RDnWR, Mul, Lp, Np_2, Tx, Erx, Ltx, In, Tm, Cmp, rom_2_data[0]}));  // open: sel
  // also tied to GND on the sheet: rom_2_data[0]

  // Other names for the same wires on the sheet: np_t = Np_2

  // Notes on the sheet:
  //   contents of rom_1 (hex, n*v repeats v):
  //   3 5 8 c d 1a e 13 15 18 10 1d f 0 b
  //   contents of rom_2 (hex, n*v repeats v):
  //   5e3000 be3000 263400 1a3000 2c3480 1a3000 2e1400 3c7000 1a3000 2e1400 3cf000 3f2480 3c7880 3cf880
  //   3a3180 3e3088 1a3000 2e1400 3e3402 1a3000 2f3080 1a3000 2e3410 3e3440 3e1420 3e3480 1a3000 2e1400
  //   3c3200 1a3004 3e3480
endmodule

module Cont_Prog (
  input  EO,
  input  CLK,
  input  CLK_EN,
  input  LOAD,
  input  D0,
  input  D1,
  input  D2,
  input  D3,
  input  CLEAR,
  output Q0,
  output Q1,
  output Q2,
  output Q3
);

  wire and_1_out, and_2_out, and_3_out, and_4_out, and_5_out, and_6_out, and_7_out, and_8_out, and_9_out,
       and_10_out, ff_t_1_q, ff_t_2_q, ff_t_3_q, ff_t_4_q, not_1_out, not_2_out, not_3_out, not_4_out;

  and and_1 (and_1_out, LOAD, D0);
  assign Q0 = EO ? ff_t_1_q : 1'bz;  // Controlled_Buffer controlled_buffer_1
  FF_T ff_t_1 (
    .T(1'b1), .CLK(CLK), .EN(CLK_EN), .Q(ff_t_1_q), .sPRE(and_1_out), .PRE(1'b0), .sCLR(and_2_out),
    .CLR(CLEAR));  // open: nQ
  and and_2 (and_2_out, LOAD, not_1_out);
  not not_1 (not_1_out, D0);
  and and_3 (and_3_out, LOAD, D1);
  FF_T ff_t_2 (
    .T(ff_t_1_q), .CLK(CLK), .EN(CLK_EN), .Q(ff_t_2_q), .sPRE(and_3_out), .PRE(1'b0), .sCLR(and_4_out),
    .CLR(CLEAR));  // open: nQ
  and and_4 (and_4_out, LOAD, not_2_out);
  not not_2 (not_2_out, D1);
  assign Q1 = EO ? ff_t_2_q : 1'bz;  // Controlled_Buffer controlled_buffer_2
  and and_5 (and_5_out, LOAD, D2);
  and and_6 (and_6_out, ff_t_1_q, ff_t_2_q);
  and and_7 (and_7_out, LOAD, not_3_out);
  not not_3 (not_3_out, D2);
  assign Q2 = EO ? ff_t_3_q : 1'bz;  // Controlled_Buffer controlled_buffer_3
  FF_T ff_t_3 (
    .T(and_6_out), .CLK(CLK), .EN(CLK_EN), .Q(ff_t_3_q), .sPRE(and_5_out), .PRE(1'b0), .sCLR(and_7_out),
    .CLR(CLEAR));  // open: nQ
  and and_8 (and_8_out, LOAD, D3);
  and and_9 (and_9_out, and_6_out, ff_t_3_q);
  and and_10 (and_10_out, LOAD, not_4_out);
  not not_4 (not_4_out, D3);
  assign Q3 = EO ? ff_t_4_q : 1'bz;  // Controlled_Buffer controlled_buffer_4
  FF_T ff_t_4 (
    .T(and_9_out), .CLK(CLK), .EN(CLK_EN), .Q(ff_t_4_q), .sPRE(and_8_out), .PRE(1'b0), .sCLR(and_10_out),
    .CLR(CLEAR));  // open: nQ
endmodule

module FF_T (
  input  sPRE,
  input  PRE,
  input  T,
  input  CLK,
  input  EN,
  input  sCLR,
  input  CLR,
  output Q,
  output nQ
);

  wire and_1_out, and_2_out, not_1_out, not_2_out, or_1_out, or_2_out;

  or or_1 (or_1_out, sPRE, T);
  not not_1 (not_1_out, sPRE);
  and and_1 (and_1_out, not_1_out, T);
  and and_2 (and_2_out, or_1_out, not_2_out);
  not not_2 (not_2_out, sCLR);
  or or_2 (or_2_out, and_1_out, sCLR);
  J_K_Flip_Flop j_k_ff_1 (.J(and_2_out), .clk(CLK), .K(or_2_out), .Q(Q), .Qn(nQ), .preset(PRE), .en(EN), .reset(CLR));
endmodule

module \Comunicação_Serial  (
  input  [7:0] Entrada,
  input  Tx,
  input  CLR,
  output [7:0] Saida
);

  wire and_1_out, clock_1_out, nand_1_out, not_1_out, not_2_out, not_3_out, or_1_out, shift_register_1_out;
  wire [3:0] counter_1_q;

  Clock clock_1 (.out(clock_1_out));
  or or_1 (or_1_out, Tx, clock_1_out);
  Shift_Register shift_register_1 (
    .shift(nand_1_out), .clk(or_1_out), .out(shift_register_1_out), .load(Tx), .d0(Entrada[7]), .q0(CLR),
    .d1(Entrada[6]), .d2(Entrada[5]), .d3(Entrada[4]), .d4(Entrada[3]), .d5(Entrada[2]), .d6(Entrada[1]),
    .d7(Entrada[0]));  // open: in, clr, q1, q2, q3, q4, q5, q6, q7
  Counter #(.width(4), .max('hf)) counter_1 (
    .Q(counter_1_q), .clk(and_1_out), .clr(CLR));  // open: load, D, count, carry
  and and_1 (and_1_out, clock_1_out, nand_1_out);
  nand nand_1 (nand_1_out, counter_1_q[3], not_1_out, not_2_out, not_3_out);
  not not_1 (not_1_out, counter_1_q[2]);
  not not_2 (not_2_out, counter_1_q[1]);
  not not_3 (not_3_out, counter_1_q[0]);
  Shift_Register shift_register_2 (
    .shift(nand_1_out), .in(shift_register_1_out), .clk(clock_1_out), .clr(CLR), .q0(Saida[7]),
    .q1(Saida[6]), .q2(Saida[5]), .q3(Saida[4]), .q4(Saida[3]), .q5(Saida[2]), .q6(Saida[1]), .q7(Saida[0]));  // open: out, load, d0, d1, d2, d3, d4, d5, d6, d7
endmodule

module TX (
  input  [3:0] Entrada,
  input  Ltx,
  input  Tx,
  input  CLK,
  input  CLR,
  output Saida,
  output HALT
);

  wire and_2_out, load, nor_1_out, not_1_out, not_2_out, or_1_out, shift_register_2_q0, shift_register_2_q1,
       shift_register_2_q2, shift_register_2_q3;

  and and_1 (HALT, Tx, not_1_out);
  not not_1 (not_1_out, load);
  or or_1 (or_1_out, Ltx, CLK);
  Shift_Register #(.length(4)) shift_register_1 (
    .shift(not_2_out), .clk(or_1_out), .out(Saida), .load(Ltx), .clr(CLR), .d0(Entrada[3]), .d1(Entrada[2]),
    .d2(Entrada[1]), .d3(Entrada[0]));  // open: in, q0, q1, q2, q3
  not not_2 (not_2_out, load);
  Shift_Register #(.length(5)) shift_register_2 (
    .in(nor_1_out), .clk(and_2_out), .clr(CLR), .q0(shift_register_2_q0), .q1(shift_register_2_q1),
    .q2(shift_register_2_q2), .q3(shift_register_2_q3), .q4(load));  // open: shift, out, load, d0, d1, d2, d3, d4
  and and_2 (and_2_out, CLK, Tx);
  nor nor_1 (nor_1_out, shift_register_2_q0, shift_register_2_q1, shift_register_2_q2, shift_register_2_q3, load);
endmodule

module RX (
  input  Entrada,
  input  CLK,
  input  Rx,
  input  CLR,
  output [3:0] Saida,
  output HALT
);

  wire and_1_out, controlled_buffer_1_out, nand_1_out, not_1_out, not_2_out, not_3_out, or_1_out;
  wire [3:0] counter_1_q, shift_register_1_q3;

  assign controlled_buffer_1_out = Rx ? CLK : 1'bz;  // Controlled_Buffer controlled_buffer_1
  Shift_Register #(.length(4)) shift_register_1 (
    .shift(nand_1_out), .in(Entrada), .clk(controlled_buffer_1_out), .clr(or_1_out),
    .q0(shift_register_1_q3[3]), .q1(shift_register_1_q3[2]), .q2(shift_register_1_q3[1]),
    .q3(shift_register_1_q3[0]));  // open: out, load, d0, d1, d2, d3
  not not_1 (not_1_out, Rx);
  or or_1 (or_1_out, CLR, not_1_out);
  and and_1 (and_1_out, controlled_buffer_1_out, nand_1_out);
  assign Saida = Rx ? shift_register_1_q3 : 4'bz;  // Controlled_Buffer controlled_buffer_2
  Counter #(.width(4), .max('hf)) counter_1 (
    .Q(counter_1_q), .clk(and_1_out), .clr(or_1_out));  // open: load, D, count, carry
  nand nand_1 (nand_1_out, not_2_out, counter_1_q[2], not_3_out, counter_1_q[0]);
  not not_2 (not_2_out, counter_1_q[3]);
  not not_3 (not_3_out, counter_1_q[1]);

  assign HALT = Rx;
endmodule

module \Unidade_de_Comunicação_Serial  (
  input  Recebendo,
  input  Enable_Rx,
  input  CLK,
  input  Erx,
  input  [3:0] Transmitimos,
  input  Enable_Tx,
  input  CLR,
  input  Ltx,
  output [3:0] DataOut,
  output HLT,
  output Transmitido
);

  wire not_1_out, rx_1_halt, tx_1_halt, tx_1_saida;
  wire [3:0] register_1_q, rx_1_saida;

  or or_1 (HLT, rx_1_halt, tx_1_halt);
  RX rx_1 (.Entrada(Recebendo), .HALT(rx_1_halt), .CLR(CLR), .Saida(rx_1_saida), .CLK(CLK), .Rx(Enable_Rx));
  TX tx_1 (
    .Entrada(Transmitimos), .Tx(Enable_Tx), .CLK(CLK), .HALT(tx_1_halt), .CLR(CLR), .Saida(tx_1_saida),
    .Ltx(Ltx));
  assign Transmitido = Enable_Tx ? tx_1_saida : 1'bz;  // Controlled_Buffer controlled_buffer_1
  Register #(.width(4)) register_1 (.D(rx_1_saida), .en(CLK), .Q(register_1_q), .clk(CLK), .clr(CLR));
  assign DataOut = not_1_out ? register_1_q : 4'bz;  // Controlled_Buffer controlled_buffer_2
  not not_1 (not_1_out, Erx);
endmodule

module Temporizador (
  input  [3:0] IN,
  input  CLK,
  input  Tm,
  input  CLR,
  output [3:0] SHOW,
  output Halt
);

  wire and_1_out, not_1_out, not_2_out, not_3_out, or_1_out, or_2_out;
  wire [3:0] multiplexer_1_out, subtractor_1_out;

  not not_1 (not_1_out, Tm);
  or or_1 (or_1_out, not_1_out, Halt);
  Multiplexer #(.width(4), .enable("false")) multiplexer_1 (
    .in0(IN), .in1(subtractor_1_out), .out(multiplexer_1_out), .sel(or_1_out));
  Counter #(.width(4), .max('hf)) counter_1 (
    .load(1'b1), .D(multiplexer_1_out), .count(not_2_out), .Q(SHOW), .clk(CLK), .clr(or_2_out));  // open: carry
  not not_2 (not_2_out, 1'b1);
  or or_2 (or_2_out, CLR, and_1_out);
  and and_1 (and_1_out, not_3_out, or_1_out);
  Subtractor #(.width(4)) subtractor_1 (.a(SHOW), .b(4'b0001), .out(subtractor_1_out));  // open: bin, bout
  not not_3 (not_3_out, Halt);
  nand nand_1 (Halt, subtractor_1_out[0], subtractor_1_out[1], subtractor_1_out[2], subtractor_1_out[3]);
endmodule
